# Fritzing sketch Part 1 Wiring Diagram (saved by Fritzing 0.9.3b)
breadboards: 1

parts:
  Raspberry_Pi_1 = Raspberry Pi 3 [part_number=RPI-3-V1.2]
  R1 = Resistor [tolerance=±5% resistance=220 package=THT]
  R2 = Resistor [tolerance=±5% resistance=220 package=THT]
  R3 = Resistor [tolerance=±5% resistance=220 package=THT]
  R4 = Resistor [tolerance=±5% resistance=220 package=THT]
  R5 = Resistor [tolerance=±5% resistance=220 package=THT]
  R6 = Resistor [tolerance=±5% resistance=220 package=THT]
  LED1 = LED - 5mm [color="Blue (470nm)" package="5 mm [THT]"]
  LED2 = LED - 5mm [color="Red (633nm)" package="5 mm [THT]"]
  LED4 = LED - 5mm [color="Blue (470nm)" package="5 mm [THT]"]
  LED5 = LED - 5mm [color="Yellow (592nm)" package="5 mm [THT]"]
  LED6 = LED - 5mm [color="Red (633nm)" package="5 mm [THT]"]
  LED7 = LED - 5mm [color="Yellow (592nm)" package="5 mm [THT]"]  # not connected

nets:
  N1: Raspberry_Pi_1.GPIO3, Raspberry_Pi_1.GND, Raspberry_Pi_1.GIPO21, R4.Pin_0
  N2: Raspberry_Pi_1.GIPO22, Raspberry_Pi_1.GIPO23, R6.Pin_0
  N3: Raspberry_Pi_1.3V3, Raspberry_Pi_1.GIPO24, R1.Pin_0
  N4: Raspberry_Pi_1.GIPO9, Raspberry_Pi_1.GIPO25, R2.Pin_0
  N5: Raspberry_Pi_1.GIPO19, Raspberry_Pi_1.GIPO16, R3.Pin_0
  N6: Raspberry_Pi_1.GIPO26, Raspberry_Pi_1.GIPO20, R5.Pin_0
  N7: R1.Pin_1, LED2.cathode
  N8: R3.Pin_1, LED4.cathode
  N9: R4.Pin_1, LED6.cathode
  N10: R5.Pin_1, LED5.cathode
  N11: R6.Pin_1, LED1.cathode
  N12: LED1.anode, LED2.anode, LED4.anode, LED5.anode, LED6.anode
