# Fritzing sketch Wiring Diagram (saved by Fritzing 0.9.3b)
breadboards: 1

parts:
  Raspberry_Pi_1 = Raspberry Pi 3 [part_number=RPI-3-V1.2]
  S1 = Pushbutton [package="[THT]"]
  J1 = Basic Servo
  R1 = Resistor [tolerance=±5% resistance=220 package=THT]

nets:
  GND: Raspberry_Pi_1.GND, S1.Pin_1, S1.Pin_2, J1.gnd
  N1: Raspberry_Pi_1.GIPO18, R1.Pin_0
  N2: Raspberry_Pi_1.GIPO15, S1.Pin_3, S1.Pin_4
  5V: Raspberry_Pi_1.5V, J1.vcc
  N3: J1.pulse, R1.Pin_1
